# Fritzing sketch CWKeyer (saved by Fritzing 1.0.6)
circuit board: 8.37863cm x 5.73501cm
breadboards: 1

parts:
  Encoder = male pin header, 5 pins [form="♂ (male)"]
  Battery = male pin header, 2 pins [form="♂ (male)"]
  Keyer = male pin header, 3 pins [form="♂ (male)"]
  Speaker = male pin header, 3 pins [form="♂ (male)"]
  Buzz = Piezo Speaker
  Display = male pin header, 4 pins [form="♂ (male)"]
  Volume = 6mm Trimmer Potentiometer [maximum_resistance=10kΩ knob_status=50% power=0.5W package=THT]
  J1 = female pin header, 15 pins [form="♀ (female)"]
  J2 = female pin header, 15 pins [form="♀ (female)"]

nets (from the pcb view):
  N1: Encoder.pin1, Keyer.pin1, Speaker.pin1, Buzz.pin2, Display.pin1, Volume.leg1, J1.pin14
  N2: Encoder.pin2, J1.pin6
  N3: Encoder.pin3, J1.pin1
  N4: Encoder.pin4, J1.pin4
  N5: Encoder.pin5, J1.pin5
  N6: Battery.pin1, J2.pin15
  N7: Battery.pin2, J2.pin14
  N8: Keyer.pin2, J1.pin9
  N9: Keyer.pin3, J1.pin10
  N10: Speaker.pin2, Speaker.pin3, Volume.wiper
  N11: Buzz.pin1, J1.pin11
  N12: Display.pin2, J1.pin15
  N13: Display.pin3, J1.pin2
  N14: Display.pin4, J1.pin3
  N15: Volume.leg2, J1.pin8

notes:
  DL1SKD
  CWKeyer
  Ver 0.4
  ESP8266
